// Logisim project t3_memory.circ as structural Verilog: 32 circuits, main circuit main
module main (
  input  RESET,
  input  START,
  input  [1:0] MODE,
  input  DOOR_CLOSED,
  input  [7:0] WATER_LEVEL,
  input  [7:0] TEMP,
  input  [7:0] DRUM_RPM,
  output VALVE_IN,
  output HEATER,
  output MOTOR_EN_REQ,
  output MOTOR_DIR,
  output PUMP_OUT,
  output DOOR_LOCK,
  output BUZZER,
  output [7:0] DISPLAY,
  output MOTOR_ACTUAL,
  output TRIP,
  output HALTED,
  output [7:0] PC,
  output V_ID,
  output V_EX,
  output V_MEM,
  output V_WB,
  output [7:0] PC_ID,
  output [7:0] PC_EX,
  output [7:0] PC_MEM,
  output [7:0] PC_WB,
  output STALL,
  output FLUSH,
  output [1:0] FWD_A,
  output [1:0] FWD_B,
  output RF_WE,
  output [2:0] RF_WA,
  output [7:0] RF_WD,
  output ST_COMMIT,
  output [7:0] ST_ADDR,
  output [7:0] ST_DATA,
  output [7:0] TMR_COUNT,
  output TMR_MATCH
);

  wire clk;

  Clock #(.highDuration(1), .lowDuration(1)) u_CLK (.out(clk));
  mcu_core core (
    .clk(clk), .rst(RESET), .start(START), .mode(MODE), .door_closed(DOOR_CLOSED), .water_level(WATER_LEVEL),
    .temp(TEMP), .drum_rpm(DRUM_RPM), .valve_in(VALVE_IN), .heater(HEATER), .motor_en(MOTOR_EN_REQ),
    .motor_dir(MOTOR_DIR), .pump_out(PUMP_OUT), .door_lock(DOOR_LOCK), .buzzer(BUZZER), .display(DISPLAY),
    .motor_actual(MOTOR_ACTUAL), .trip(TRIP), .halted(HALTED), .pc(PC), .ifid_v(V_ID), .idex_v(V_EX),
    .exm_v(V_MEM), .mwb_v(V_WB), .ifid_pc(PC_ID), .idex_pc(PC_EX), .exm_pc(PC_MEM), .mwb_pc(PC_WB),
    .stall(STALL), .flush(FLUSH), .fwd_a(FWD_A), .fwd_b(FWD_B), .rf_we(RF_WE), .rf_wa(RF_WA), .rf_wd(RF_WD),
    .st_commit(ST_COMMIT), .st_addr(ST_ADDR), .st_data(ST_DATA), .tmr_count(TMR_COUNT), .tmr_match(TMR_MATCH));

  // Notes on the sheet:
  //   WASHING-MACHINE PIPELINED MCU (top level)
  //   Inputs: RESET (hold 1 then 0), START, MODE[1:0], DOOR_CLOSED, WATER_LEVEL, TEMP, DRUM_RPM.  Clock: Simulate > Ticks Enabled.
  //   Outputs: commanded actuators, MOTOR_ACTUAL (safety-gated), TRIP, DISPLAY, HALTED and pipeline debug probes.
endmodule

module mux2_1 (
  input  a,
  input  b,
  input  s,
  output y
);

  wire n1, t2, t3;

  not not_1 (n1, s);
  and and_1 (t3, b, s);
  and and_2 (t2, a, n1);
  or or_1 (y, t2, t3);

  // Notes on the sheet:
  //   MUX2 x1
endmodule

module mux2_3 (
  input  [2:0] a,
  input  [2:0] b,
  input  s,
  output [2:0] y
);

  wire [2:0] ns_bus, t1, t2;

  assign t1 = a & ns_bus;  // AND_Gate and_1, 3 bits wide
  assign y = t1 | t2;  // OR_Gate or_1, 3 bits wide
  assign ns_bus = ~{3{s}};  // NOT_Gate not_1, 3 bits wide
  assign t2 = b & {3{s}};  // AND_Gate and_2, 3 bits wide

  // Other names for the same wires on the sheet: s_bus[2:0] = {3{s}}

  // Notes on the sheet:
  //   MUX2 x3
  //   y = s ? b : a   (sel bit replicated with a splitter, then AND-OR)
endmodule

module mux2_8 (
  input  [7:0] a,
  input  [7:0] b,
  input  s,
  output [7:0] y
);

  wire [7:0] ns_bus, t1, t2;

  assign t1 = a & ns_bus;  // AND_Gate and_1, 8 bits wide
  assign y = t1 | t2;  // OR_Gate or_1, 8 bits wide
  assign ns_bus = ~{8{s}};  // NOT_Gate not_1, 8 bits wide
  assign t2 = b & {8{s}};  // AND_Gate and_2, 8 bits wide

  // Other names for the same wires on the sheet: s_bus[7:0] = {8{s}}

  // Notes on the sheet:
  //   MUX2 x8
  //   y = s ? b : a   (sel bit replicated with a splitter, then AND-OR)
endmodule

module mux4_8 (
  input  [7:0] a0,
  input  [7:0] a1,
  input  [7:0] a2,
  input  [7:0] a3,
  input  [1:0] s,
  output [7:0] y
);

  wire [7:0] m0, m1;

  mux2_8 m_hi (.a(a2), .b(a3), .s(s[0]), .y(m1));
  mux2_8 m_lo (.a(a0), .b(a1), .s(s[0]), .y(m0));
  mux2_8 m_out (.a(m0), .b(m1), .s(s[1]), .y(y));

  // Other names for the same wires on the sheet: s_0 = s[0]; s_1 = s[1]

  // Notes on the sheet:
  //   MUX4 x8
endmodule

module mux8_8 (
  input  [7:0] a0,
  input  [7:0] a1,
  input  [7:0] a2,
  input  [7:0] a3,
  input  [7:0] a4,
  input  [7:0] a5,
  input  [7:0] a6,
  input  [7:0] a7,
  input  [2:0] s,
  output [7:0] y
);

  wire [7:0] m0, m1;

  mux4_8 q_lo (.a0(a0), .a1(a1), .a2(a2), .a3(a3), .s(s[1:0]), .y(m0));
  mux2_8 m_out (.a(m0), .b(m1), .s(s[2]), .y(y));
  mux4_8 q_hi (.a0(a4), .a1(a5), .a2(a6), .a3(a7), .s(s[1:0]), .y(m1));

  // Other names for the same wires on the sheet: s_lo[1:0] = s[1:0]

  // Notes on the sheet:
  //   MUX8 x8
endmodule

module dec3to8 (
  input  [2:0] a,
  input  en,
  output [7:0] y
);

  wire na0, na1, na2;

  not not_1 (na2, a[2]);
  and and_1 (y[2], en, na0, a[1], na2);
  and and_2 (y[4], en, na0, na1, a[2]);
  and and_3 (y[6], en, na0, a[1], a[2]);
  not not_2 (na0, a[0]);
  and and_4 (y[0], en, na0, na1, na2);
  and and_5 (y[3], en, a[0], a[1], na2);
  and and_6 (y[5], en, a[0], na1, a[2]);
  and and_7 (y[7], en, a[0], a[1], a[2]);
  not not_3 (na1, a[1]);
  and and_8 (y[1], en, a[0], na1, na2);

  // Other names for the same wires on the sheet: a_0 = a[0]; a_1 = a[1]; a_2 = a[2]

  // Notes on the sheet:
  //   DEC 3-to-8
endmodule

module dec4to16 (
  input  [3:0] a,
  input  en,
  output [15:0] y
);

  wire na0, na1, na2, na3;

  not not_1 (na3, a[3]);
  and and_1 (y[3], en, a[0], a[1], na2, na3);
  and and_2 (y[6], en, na0, a[1], a[2], na3);
  and and_3 (y[9], en, a[0], na1, na2, a[3]);
  and and_4 (y[12], en, na0, na1, a[2], a[3]);
  and and_5 (y[15], en, a[0], a[1], a[2], a[3]);
  not not_2 (na0, a[0]);
  and and_6 (y[0], en, na0, na1, na2, na3);
  and and_7 (y[4], en, na0, na1, a[2], na3);
  and and_8 (y[7], en, a[0], a[1], a[2], na3);
  and and_9 (y[10], en, na0, a[1], na2, a[3]);
  and and_10 (y[13], en, a[0], na1, a[2], a[3]);
  not not_3 (na1, a[1]);
  and and_11 (y[1], en, a[0], na1, na2, na3);
  and and_12 (y[5], en, a[0], na1, a[2], na3);
  and and_13 (y[8], en, na0, na1, na2, a[3]);
  and and_14 (y[11], en, a[0], a[1], na2, a[3]);
  and and_15 (y[14], en, na0, a[1], a[2], a[3]);
  not not_4 (na2, a[2]);
  and and_16 (y[2], en, na0, a[1], na2, na3);

  // Other names for the same wires on the sheet: a_0 = a[0]; a_1 = a[1]; a_2 = a[2]; a_3 = a[3]

  // Notes on the sheet:
  //   DEC 4-to-16
endmodule

module eq3 (
  input  [2:0] a,
  input  [2:0] b,
  output eq
);

  wire any;
  wire [2:0] diff;

  assign diff = a ^ b;  // XOR_Gate xor_1, 3 bits wide
  or or_1 (any, diff[0], diff[1], diff[2]);
  not not_1 (eq, any);

  // Other names for the same wires on the sheet: diff_0 = diff[0]; diff_1 = diff[1]; diff_2 = diff[2]

  // Notes on the sheet:
  //   EQ x3
  //   eq = NOR(a XOR b)
endmodule

module eq8 (
  input  [7:0] a,
  input  [7:0] b,
  output eq
);

  wire any;
  wire [7:0] diff;

  assign diff = a ^ b;  // XOR_Gate xor_1, 8 bits wide
  or or_1 (any, diff[0], diff[1], diff[2], diff[3], diff[4], diff[5], diff[6], diff[7]);
  not not_1 (eq, any);

  // Other names for the same wires on the sheet: diff_0 = diff[0]; diff_1 = diff[1]; diff_2 = diff[2];
  //   diff_3 = diff[3]; diff_4 = diff[4]; diff_5 = diff[5]; diff_6 = diff[6]; diff_7 = diff[7]

  // Notes on the sheet:
  //   EQ x8
  //   eq = NOR(a XOR b)
endmodule

module zero8 (
  input  [7:0] a,
  output z
);

  wire any;

  not not_1 (z, any);
  or or_1 (any, a[0], a[1], a[2], a[3], a[4], a[5], a[6], a[7]);

  // Other names for the same wires on the sheet: a_0 = a[0]; a_1 = a[1]; a_2 = a[2]; a_3 = a[3]; a_4 = a[4];
  //   a_5 = a[5]; a_6 = a[6]; a_7 = a[7]

  // Notes on the sheet:
  //   ZERO x8
endmodule

module half_add (
  input  a,
  input  b,
  output s,
  output co
);

  xor xor_1 (s, a, b);
  and and_1 (co, a, b);

  // Notes on the sheet:
  //   HALF ADDER
endmodule

module full_add (
  input  a,
  input  b,
  input  ci,
  output s,
  output co
);

  wire p, t1, t2;

  xor xor_1 (p, a, b);
  and and_1 (t1, a, b);
  or or_1 (co, t1, t2);
  xor xor_2 (s, p, ci);
  and and_2 (t2, p, ci);

  // Notes on the sheet:
  //   FULL ADDER
endmodule

module add8 (
  input  [7:0] a,
  input  [7:0] b,
  input  ci,
  output [7:0] s,
  output co
);

  wire c1, c2, c3, c4, c5, c6, c7;

  full_add fa1 (.a(a[1]), .b(b[1]), .ci(c1), .s(s[1]), .co(c2));
  full_add fa4 (.a(a[4]), .b(b[4]), .ci(c4), .s(s[4]), .co(c5));
  full_add fa7 (.a(a[7]), .b(b[7]), .ci(c7), .s(s[7]), .co(co));
  full_add fa2 (.a(a[2]), .b(b[2]), .ci(c2), .s(s[2]), .co(c3));
  full_add fa5 (.a(a[5]), .b(b[5]), .ci(c5), .s(s[5]), .co(c6));
  full_add fa0 (.a(a[0]), .b(b[0]), .ci(ci), .s(s[0]), .co(c1));
  full_add fa3 (.a(a[3]), .b(b[3]), .ci(c3), .s(s[3]), .co(c4));
  full_add fa6 (.a(a[6]), .b(b[6]), .ci(c6), .s(s[6]), .co(c7));

  // Other names for the same wires on the sheet: a_0 = a[0]; a_1 = a[1]; a_2 = a[2]; a_3 = a[3]; a_4 = a[4];
  //   a_5 = a[5]; a_6 = a[6]; a_7 = a[7]; b_0 = b[0]; b_1 = b[1]; b_2 = b[2]; b_3 = b[3]; b_4 = b[4]; b_5 = b[5];
  //   b_6 = b[6]; b_7 = b[7]; s_0 = s[0]; s_1 = s[1]; s_2 = s[2]; s_3 = s[3]; s_4 = s[4]; s_5 = s[5]; s_6 = s[6];
  //   s_7 = s[7]

  // Notes on the sheet:
  //   ADD8 ripple
endmodule

module inc8 (
  input  [7:0] a,
  output [7:0] y,
  output co
);

  wire c1, c2, c3, c4, c5, c6, c7;

  half_add ha1 (.a(a[1]), .b(c1), .s(y[1]), .co(c2));
  half_add ha3 (.a(a[3]), .b(c3), .s(y[3]), .co(c4));
  half_add ha5 (.a(a[5]), .b(c5), .s(y[5]), .co(c6));
  half_add ha7 (.a(a[7]), .b(c7), .s(y[7]), .co(co));
  half_add ha2 (.a(a[2]), .b(c2), .s(y[2]), .co(c3));
  half_add ha4 (.a(a[4]), .b(c4), .s(y[4]), .co(c5));
  half_add ha6 (.a(a[6]), .b(c6), .s(y[6]), .co(c7));
  half_add ha0 (.a(a[0]), .b(1'b1), .s(y[0]), .co(c1));

  // Other names for the same wires on the sheet: a_0 = a[0]; a_1 = a[1]; a_2 = a[2]; a_3 = a[3]; a_4 = a[4];
  //   a_5 = a[5]; a_6 = a[6]; a_7 = a[7]; y_0 = y[0]; y_1 = y[1]; y_2 = y[2]; y_3 = y[3]; y_4 = y[4]; y_5 = y[5];
  //   y_6 = y[6]; y_7 = y[7]

  // Notes on the sheet:
  //   INC8 (+1)
endmodule

module alu8 (
  input  [7:0] x,
  input  [7:0] y,
  input  [1:0] op,
  input  sub,
  output [7:0] r,
  output cout
);

  wire lt_u;
  wire [7:0] and_xy, sum, y_inv;

  add8 adder (.a(x), .b(y_inv), .ci(sub), .s(sum), .co(cout));
  mux4_8 result_mux (.a0(sum), .a1(and_xy), .a2(y), .a3({{7{1'b0}}, lt_u}), .s(op), .y(r));
  not not_1 (lt_u, cout);
  assign y_inv = y ^ {8{sub}};  // XOR_Gate xor_1, 8 bits wide
  assign and_xy = x & y;  // AND_Gate and_1, 8 bits wide

  // Other names for the same wires on the sheet: sltu_v[0] = lt_u; sub_bus[7:0] = {8{sub}}

  // Notes on the sheet:
  //   ALU8
  //   op: 00 = x + (y^sub) + sub   01 = x AND y   10 = pass y   11 = SLTU {7'b0, ~cout}
  //   SUB/SLTU set sub=1: x + ~y + 1, so cout = 1 exactly when x >= y (unsigned)
endmodule

module regfile8x8 (
  input  clk,
  input  [2:0] ra,
  input  [2:0] rb,
  input  [2:0] wa,
  input  [7:0] wd,
  input  we,
  output [7:0] qa,
  output [7:0] qb,
  output [7:0] r0,
  output [7:0] r1,
  output [7:0] r2,
  output [7:0] r3,
  output [7:0] r4,
  output [7:0] r5,
  output [7:0] r6,
  output [7:0] r7
);

  wire byp_a, byp_b, eq_a, eq_b, wen_0, wen_1, wen_2, wen_3, wen_4, wen_5, wen_6, wen_7;
  wire [7:0] raw_a, raw_b;

  dec3to8 wdec (.a(wa), .en(we), .y({wen_7, wen_6, wen_5, wen_4, wen_3, wen_2, wen_1, wen_0}));
  eq3 cmp_a (.a(ra), .b(wa), .eq(eq_a));
  mux2_8 bypass_a (.a(raw_a), .b(wd), .s(byp_a), .y(qa));
  Register #(.width(8), .trigger("rising")) u_R2 (.D(wd), .en(wen_2), .Q(r2), .clk(clk));  // open: clr
  Register #(.width(8), .trigger("rising")) u_R6 (.D(wd), .en(wen_6), .Q(r6), .clk(clk));  // open: clr
  eq3 cmp_b (.a(rb), .b(wa), .eq(eq_b));
  mux2_8 bypass_b (.a(raw_b), .b(wd), .s(byp_b), .y(qb));
  Register #(.width(8), .trigger("rising")) u_R3 (.D(wd), .en(wen_3), .Q(r3), .clk(clk));  // open: clr
  Register #(.width(8), .trigger("rising")) u_R7 (.D(wd), .en(wen_7), .Q(r7), .clk(clk));  // open: clr
  mux8_8 read_a (.a0(r0), .a1(r1), .a2(r2), .a3(r3), .a4(r4), .a5(r5), .a6(r6), .a7(r7), .s(ra), .y(raw_a));
  and and_1 (byp_a, eq_a, we);
  Register #(.width(8), .trigger("rising")) u_R0 (.D(wd), .en(wen_0), .Q(r0), .clk(clk));  // open: clr
  Register #(.width(8), .trigger("rising")) u_R4 (.D(wd), .en(wen_4), .Q(r4), .clk(clk));  // open: clr
  mux8_8 read_b (.a0(r0), .a1(r1), .a2(r2), .a3(r3), .a4(r4), .a5(r5), .a6(r6), .a7(r7), .s(rb), .y(raw_b));
  and and_2 (byp_b, eq_b, we);
  Register #(.width(8), .trigger("rising")) u_R1 (.D(wd), .en(wen_1), .Q(r1), .clk(clk));  // open: clr
  Register #(.width(8), .trigger("rising")) u_R5 (.D(wd), .en(wen_5), .Q(r5), .clk(clk));  // open: clr

  // Other names for the same wires on the sheet: wsel[7:0] = {wen_7, wen_6, wen_5, wen_4, wen_3, wen_2, wen_1, wen_0}

  // Notes on the sheet:
  //   REGISTER FILE 8x8
  //   Eight 8-bit Registers (R0..R7, none hardwired).  Write on rising edge when we=1.
  //   Write-through bypass: a WB write to the register being read appears on qa/qb in the same cycle.
endmodule

module if_id (
  input  clk,
  input  rst,
  input  en,
  input  v_d,
  input  [7:0] pc_d,
  input  [15:0] ir_d,
  output v,
  output [7:0] pc,
  output [15:0] ir
);

  Register #(.width(1), .trigger("rising")) u_v (.D(v_d), .en(en), .Q(v), .clk(clk), .clr(rst));
  Register #(.width(16), .trigger("rising")) u_ir (.D(ir_d), .en(en), .Q(ir), .clk(clk), .clr(rst));
  Register #(.width(8), .trigger("rising")) u_pc (.D(pc_d), .en(en), .Q(pc), .clk(clk), .clr(rst));

  // Notes on the sheet:
  //   IF/ID REGISTER
  //   Every field is a rising-edge Register cleared by reset (valid=0 after reset).
endmodule

module id_ex (
  input  clk,
  input  rst,
  input  v_d,
  input  [7:0] pc_d,
  input  [2:0] rd_d,
  input  [2:0] rb_d,
  input  [7:0] a_d,
  input  [7:0] b_d,
  input  [7:0] imm_d,
  input  [1:0] aluop_d,
  input  alusub_d,
  input  aluimm_d,
  input  regw_d,
  input  memr_d,
  input  memw_d,
  input  beqz_d,
  input  bnez_d,
  input  jmp_d,
  input  halt_d,
  output v,
  output [7:0] pc,
  output [2:0] rd,
  output [2:0] rb,
  output [7:0] a,
  output [7:0] b,
  output [7:0] imm,
  output [1:0] aluop,
  output alusub,
  output aluimm,
  output regw,
  output memr,
  output memw,
  output beqz,
  output bnez,
  output jmp,
  output halt
);

  Register #(.width(1), .trigger("rising")) u_v (.D(v_d), .Q(v), .clk(clk), .clr(rst));  // open: en
  Register #(.width(8), .trigger("rising")) u_b (.D(b_d), .Q(b), .clk(clk), .clr(rst));  // open: en
  Register #(.width(1), .trigger("rising")) u_aluimm (.D(aluimm_d), .Q(aluimm), .clk(clk), .clr(rst));  // open: en
  Register #(.width(1), .trigger("rising")) u_beqz (.D(beqz_d), .Q(beqz), .clk(clk), .clr(rst));  // open: en
  Register #(.width(8), .trigger("rising")) u_pc (.D(pc_d), .Q(pc), .clk(clk), .clr(rst));  // open: en
  Register #(.width(8), .trigger("rising")) u_imm (.D(imm_d), .Q(imm), .clk(clk), .clr(rst));  // open: en
  Register #(.width(1), .trigger("rising")) u_bnez (.D(bnez_d), .Q(bnez), .clk(clk), .clr(rst));  // open: en
  Register #(.width(1), .trigger("rising")) u_regw (.D(regw_d), .Q(regw), .clk(clk), .clr(rst));  // open: en
  Register #(.width(3), .trigger("rising")) u_rd (.D(rd_d), .Q(rd), .clk(clk), .clr(rst));  // open: en
  Register #(.width(2), .trigger("rising")) u_aluop (.D(aluop_d), .Q(aluop), .clk(clk), .clr(rst));  // open: en
  Register #(.width(1), .trigger("rising")) u_memr (.D(memr_d), .Q(memr), .clk(clk), .clr(rst));  // open: en
  Register #(.width(1), .trigger("rising")) u_jmp (.D(jmp_d), .Q(jmp), .clk(clk), .clr(rst));  // open: en
  Register #(.width(3), .trigger("rising")) u_rb (.D(rb_d), .Q(rb), .clk(clk), .clr(rst));  // open: en
  Register #(.width(1), .trigger("rising")) u_alusub (.D(alusub_d), .Q(alusub), .clk(clk), .clr(rst));  // open: en
  Register #(.width(1), .trigger("rising")) u_halt (.D(halt_d), .Q(halt), .clk(clk), .clr(rst));  // open: en
  Register #(.width(8), .trigger("rising")) u_a (.D(a_d), .Q(a), .clk(clk), .clr(rst));  // open: en
  Register #(.width(1), .trigger("rising")) u_memw (.D(memw_d), .Q(memw), .clk(clk), .clr(rst));  // open: en

  // Notes on the sheet:
  //   ID/EX REGISTER
  //   Every field is a rising-edge Register cleared by reset (valid=0 after reset).
endmodule

module ex_mem (
  input  clk,
  input  rst,
  input  v_d,
  input  [7:0] pc_d,
  input  [2:0] rd_d,
  input  [7:0] res_d,
  input  [7:0] addr_d,
  input  [7:0] sdata_d,
  input  regw_d,
  input  memr_d,
  input  memw_d,
  output v,
  output [7:0] pc,
  output [2:0] rd,
  output [7:0] res,
  output [7:0] addr,
  output [7:0] sdata,
  output regw,
  output memr,
  output memw
);

  Register #(.width(1), .trigger("rising")) u_v (.D(v_d), .Q(v), .clk(clk), .clr(rst));  // open: en
  Register #(.width(8), .trigger("rising")) u_addr (.D(addr_d), .Q(addr), .clk(clk), .clr(rst));  // open: en
  Register #(.width(1), .trigger("rising")) u_memr (.D(memr_d), .Q(memr), .clk(clk), .clr(rst));  // open: en
  Register #(.width(8), .trigger("rising")) u_pc (.D(pc_d), .Q(pc), .clk(clk), .clr(rst));  // open: en
  Register #(.width(8), .trigger("rising")) u_sdata (.D(sdata_d), .Q(sdata), .clk(clk), .clr(rst));  // open: en
  Register #(.width(1), .trigger("rising")) u_memw (.D(memw_d), .Q(memw), .clk(clk), .clr(rst));  // open: en
  Register #(.width(3), .trigger("rising")) u_rd (.D(rd_d), .Q(rd), .clk(clk), .clr(rst));  // open: en
  Register #(.width(1), .trigger("rising")) u_regw (.D(regw_d), .Q(regw), .clk(clk), .clr(rst));  // open: en
  Register #(.width(8), .trigger("rising")) u_res (.D(res_d), .Q(res), .clk(clk), .clr(rst));  // open: en

  // Notes on the sheet:
  //   EX/MEM REGISTER
  //   Every field is a rising-edge Register cleared by reset (valid=0 after reset).
endmodule

module mem_wb (
  input  clk,
  input  rst,
  input  v_d,
  input  [7:0] pc_d,
  input  [2:0] rd_d,
  input  [7:0] wdata_d,
  input  regw_d,
  output v,
  output [7:0] pc,
  output [2:0] rd,
  output [7:0] wdata,
  output regw
);

  Register #(.width(1), .trigger("rising")) u_v (.D(v_d), .Q(v), .clk(clk), .clr(rst));  // open: en
  Register #(.width(8), .trigger("rising")) u_wdata (.D(wdata_d), .Q(wdata), .clk(clk), .clr(rst));  // open: en
  Register #(.width(8), .trigger("rising")) u_pc (.D(pc_d), .Q(pc), .clk(clk), .clr(rst));  // open: en
  Register #(.width(1), .trigger("rising")) u_regw (.D(regw_d), .Q(regw), .clk(clk), .clr(rst));  // open: en
  Register #(.width(3), .trigger("rising")) u_rd (.D(rd_d), .Q(rd), .clk(clk), .clr(rst));  // open: en

  // Notes on the sheet:
  //   MEM/WB REGISTER
  //   Every field is a rising-edge Register cleared by reset (valid=0 after reset).
endmodule

module control_dec (
  input  [3:0] op,
  output regw,
  output aluimm,
  output [1:0] aluop,
  output alusub,
  output memr,
  output memw,
  output beqz,
  output bnez,
  output jmp,
  output halt,
  output uses_a,
  output uses_b
);

  wire is_0, is_1, is_2, is_3, is_4, is_5, is_6, is_7, is_8, is_9, is_10, is_11, is_12, is_13, is_14, is_15;

  or or_1 (aluop[0], is_5, is_12);
  or or_2 (memr, is_6, is_6);
  or or_3 (jmp, is_11, is_11);
  dec4to16 opdec (
    .a(op), .en(1'b1),
    .y({is_15, is_14, is_13, is_12, is_11, is_10, is_9, is_8, is_7, is_6, is_5, is_4, is_3, is_2, is_1, is_0}));
  or or_4 (regw, is_1, is_2, is_3, is_4, is_5, is_6, is_8, is_12);
  or or_5 (uses_b, is_2, is_3, is_4, is_5, is_6, is_7, is_12);
  or or_6 (aluimm, is_1, is_8);
  or or_7 (memw, is_7, is_7);
  or or_8 (halt, is_15, is_15);
  or or_9 (beqz, is_9, is_9);
  or or_10 (aluop[1], is_1, is_2, is_12);
  or or_11 (alusub, is_4, is_12);
  or or_12 (uses_a, is_3, is_4, is_5, is_7, is_8, is_9, is_10, is_12);
  or or_13 (bnez, is_10, is_10);

  // Other names for the same wires on the sheet: onehot[15:0] = {is_15, is_14, is_13, is_12, is_11, is_10, is_9, is_8, is_7, is_6, is_5, is_4, is_3, is_2, is_1, is_0}

  // Notes on the sheet:
  //   CONTROL DECODER (ID)
  //   Opcodes: 0 NOP 1 LDI 2 MOV 3 ADD 4 SUB 5 AND 6 LD 7 ST 8 ADDI 9 BEQZ A BNEZ B JMP C SLTU F HALT
  //   D, E reserved: decode to no control bits = NOP (no register/RAM/I-O write).
endmodule

module hazard_unit (
  input  ifid_v,
  input  [2:0] ra,
  input  [2:0] rb,
  input  uses_a,
  input  uses_b,
  input  idex_v,
  input  idex_memr,
  input  [2:0] idex_rd,
  output stall
);

  wire dep, dep_a, dep_b, eq_a, eq_b;

  eq3 cmp_a (.a(ra), .b(idex_rd), .eq(eq_a));
  and and_1 (dep_a, uses_a, eq_a);
  or or_1 (dep, dep_a, dep_b);
  and and_2 (stall, ifid_v, idex_v, idex_memr, dep);
  eq3 cmp_b (.a(rb), .b(idex_rd), .eq(eq_b));
  and and_3 (dep_b, uses_b, eq_b);

  // Notes on the sheet:
  //   LOAD-USE HAZARD DETECT
  //   stall = IF/ID.v & ID/EX.v & ID/EX.memr & ((uses_a & ra==ID/EX.rd) | (uses_b & rb==ID/EX.rd))
endmodule

module pipe_ctrl (
  input  stall,
  input  taken,
  input  halt_ex,
  input  halted,
  input  ifid_v,
  output kill,
  output stall_eff,
  output pc_en,
  output ifid_en,
  output ifid_vd,
  output idex_vd,
  output halted_d
);

  wire bubble, no_fetch, not_bubble, not_hold, not_kill, pc_hold;

  not not_1 (not_hold, pc_hold);
  not not_2 (not_bubble, bubble);
  or or_1 (kill, taken, halt_ex);
  and and_1 (stall_eff, stall, not_kill);
  not not_3 (ifid_en, stall_eff);
  not not_4 (ifid_vd, no_fetch);
  or or_2 (halted_d, halted, halt_ex);
  not not_5 (not_kill, kill);
  or or_3 (pc_hold, stall_eff, halt_ex, halted);
  or or_4 (pc_en, taken, not_hold);
  or or_5 (no_fetch, kill, halted);
  or or_6 (bubble, kill, stall);
  and and_2 (idex_vd, ifid_v, not_bubble);

  // Notes on the sheet:
  //   PIPELINE CONTROL (stall / flush / halt)
  //   kill = taken | halt_ex  (flush IF/ID and ID/EX) ; flush has priority over a younger stall
  //   stall_eff = stall & ~kill ; PC/IF-ID freeze on stall_eff ; ID/EX gets a bubble
endmodule

module fwd_unit (
  input  [2:0] src_a,
  input  [2:0] src_b,
  input  [7:0] a_rf,
  input  [7:0] b_rf,
  input  exm_v,
  input  exm_regw,
  input  exm_memr,
  input  [2:0] exm_rd,
  input  [7:0] exm_res,
  input  mwb_v,
  input  mwb_regw,
  input  [2:0] mwb_rd,
  input  [7:0] mwb_wd,
  output [7:0] a_fwd,
  output [7:0] b_fwd,
  output [1:0] fwd_a,
  output [1:0] fwd_b
);

  wire a_eq_exm, a_eq_mwb, a_hit_exm, a_no_exm, b_eq_exm, b_eq_mwb, b_hit_exm, b_no_exm, exm_fwdable,
       exm_not_load, exm_writer, mwb_writer;
  wire [7:0] a_m1, b_m1;

  and and_1 (exm_writer, exm_v, exm_regw);
  and and_2 (mwb_writer, mwb_v, mwb_regw);
  and and_3 (a_hit_exm, exm_writer, a_eq_exm);
  and and_4 (fwd_a[0], mwb_writer, a_eq_mwb, a_no_exm);
  and and_5 (b_hit_exm, exm_writer, b_eq_exm);
  and and_6 (fwd_b[0], mwb_writer, b_eq_mwb, b_no_exm);
  not not_1 (exm_not_load, exm_memr);
  eq3 cmp_a_exm (.a(src_a), .b(exm_rd), .eq(a_eq_exm));
  mux2_8 mux_a_wb (.a(a_rf), .b(mwb_wd), .s(fwd_a[0]), .y(a_m1));
  eq3 cmp_b_exm (.a(src_b), .b(exm_rd), .eq(b_eq_exm));
  mux2_8 mux_b_wb (.a(b_rf), .b(mwb_wd), .s(fwd_b[0]), .y(b_m1));
  and and_7 (fwd_a[1], exm_fwdable, a_eq_exm);
  and and_8 (fwd_b[1], exm_fwdable, b_eq_exm);
  eq3 cmp_a_mwb (.a(src_a), .b(mwb_rd), .eq(a_eq_mwb));
  and and_9 (exm_fwdable, exm_writer, exm_not_load);
  not not_2 (a_no_exm, a_hit_exm);
  mux2_8 mux_a_ex (.a(a_m1), .b(exm_res), .s(fwd_a[1]), .y(a_fwd));
  eq3 cmp_b_mwb (.a(src_b), .b(mwb_rd), .eq(b_eq_mwb));
  not not_3 (b_no_exm, b_hit_exm);
  mux2_8 mux_b_ex (.a(b_m1), .b(exm_res), .s(fwd_b[1]), .y(b_fwd));

  // Other names for the same wires on the sheet: a_sel_mwb = fwd_a[0]; a_sel_exm = fwd_a[1]; b_sel_mwb = fwd_b[0];
  //   b_sel_exm = fwd_b[1]

  // Notes on the sheet:
  //   FORWARDING UNIT (EX)
  //   Youngest writer wins: EX/MEM (if not a load) before MEM/WB; a load in EX/MEM is never forwarded.
  //   fwd code: 00 = register file, 01 = MEM/WB, 10 = EX/MEM
endmodule

module ex_stage (
  input  [7:0] a,
  input  [7:0] b,
  input  [7:0] imm,
  input  [1:0] aluop,
  input  alusub,
  input  aluimm,
  input  v,
  input  beqz,
  input  bnez,
  input  jmp,
  input  halt,
  output [7:0] res,
  output taken,
  output halt_ex,
  output a_zero
);

  wire a_nonzero, beqz_t, bnez_t, cond, cout;
  wire [7:0] alu_y;

  zero8 ztest (.a(a), .z(a_zero));
  mux2_8 y_sel (.a(b), .b(imm), .s(aluimm), .y(alu_y));
  and and_1 (halt_ex, v, halt);
  and and_2 (beqz_t, beqz, a_zero);
  or or_1 (cond, jmp, beqz_t, bnez_t);
  alu8 alu (.x(a), .y(alu_y), .op(aluop), .sub(alusub), .r(res), .cout(cout));
  not not_1 (a_nonzero, a_zero);
  and and_3 (taken, v, cond);
  and and_4 (bnez_t, bnez, a_nonzero);

  // Notes on the sheet:
  //   EX STAGE: ALU + branch resolution
  //   Y = aluimm ? imm : b ; taken = v & (jmp | beqz & (a==0) | bnez & (a!=0)) ; target = imm
endmodule

module timer8 (
  input  clk,
  input  rst,
  input  wr_limit,
  input  wr_ctrl,
  input  [7:0] wdata,
  output [7:0] count,
  output [7:0] limit,
  output en,
  output match
);

  wire clr_cmd, count_en, hit, inc_eq_limit, limit_nonzero, limit_zero, match_d, match_or, wrap;
  wire [7:0] count_d, count_inc;
  wire [7:7] nclr_bus;

  not not_1 (limit_nonzero, limit_zero);
  and and_1 (match_d, match_or, nclr_bus[7]);
  Register #(.width(8), .trigger("rising")) TIMER_LIMIT (.D(wdata), .en(wr_limit), .Q(limit), .clk(clk), .clr(rst));
  Register #(.width(8), .trigger("rising")) TIMER_COUNT (.D(count_d), .en(count_en), .Q(count), .clk(clk), .clr(rst));
  and and_2 (clr_cmd, wr_ctrl, wdata[1]);
  eq8 cmp (.a(count_inc), .b(limit), .eq(inc_eq_limit));
  Register #(.width(1), .trigger("rising")) TIMER_MATCH (.D(match_d), .Q(match), .clk(clk), .clr(rst));  // open: en
  Register #(.width(1), .trigger("rising")) TIMER_EN (.D(wdata[0]), .en(wr_ctrl), .Q(en), .clk(clk), .clr(rst));
  assign count_d = count_inc & {8{nclr_bus[7]}};  // AND_Gate and_3, 8 bits wide
  and and_4 (hit, en, inc_eq_limit, limit_nonzero);
  not not_2 (nclr_bus[7], clr_cmd);
  inc8 incr (.a(count), .y(count_inc), .co(wrap));
  or or_1 (count_en, clr_cmd, en);
  zero8 limz (.a(limit), .z(limit_zero));
  or or_2 (match_or, match, hit);

  // Other names for the same wires on the sheet: nclr_bus[6:0] = {7{nclr_bus[7]}}; not_clr = nclr_bus[7];
  //   wd_0 = wdata[0]; wd_1 = wdata[1]; wd_2 = wdata[2]; wd_3 = wdata[3]; wd_4 = wdata[4]; wd_5 = wdata[5];
  //   wd_6 = wdata[6]; wd_7 = wdata[7]

  // Notes on the sheet:
  //   TIMER (8-bit, free running on CLK)
  //   Ticks on every rising CLK edge, independent of CPU stall/halt.  CTRL write: bit0 = EN, bit1 = CLR (pulse).
  //   clr has priority: COUNT<=0, MATCH<=0.  Else if EN: COUNT<=COUNT+1 and MATCH |= (COUNT+1 == LIMIT != 0).
endmodule

module safety_ilock (
  input  clk,
  input  rst,
  input  motor_req,
  input  door_closed,
  input  start,
  output motor_actual,
  output trip
);

  wire door_open, not_rearm, not_start_prev, not_trip, rearm, req_off, start_prev, start_rise, trip_d,
       trip_hold, trip_set;

  Register #(.width(1), .trigger("rising")) u_START_PREV (.D(start), .Q(start_prev), .clk(clk), .clr(rst));  // open: en
  not not_1 (req_off, motor_req);
  Register #(.width(1), .trigger("rising")) u_TRIP (.D(trip_d), .Q(trip), .clk(clk), .clr(rst));  // open: en
  and and_1 (start_rise, start, not_start_prev);
  and and_2 (trip_hold, trip, not_rearm);
  and and_3 (rearm, trip, req_off, door_closed, start_rise);
  not not_2 (not_start_prev, start_prev);
  not not_3 (not_trip, trip);
  and and_4 (trip_set, motor_req, door_open);
  or or_1 (trip_d, trip_set, trip_hold);
  not not_4 (door_open, door_closed);
  not not_5 (not_rearm, rearm);
  and and_5 (motor_actual, motor_req, door_closed, not_trip);

  // Notes on the sheet:
  //   SAFETY INTERLOCK (hardware)
  //   motor_actual = motor_req & door_closed & ~trip   (purely combinational door gate)
  //   TRIP <= set | (TRIP & ~rearm) ; set = motor_req & ~door_closed (sampled on CLK)
  //   rearm = TRIP & ~motor_req & door_closed & START rising edge (start & ~start_prev)
endmodule

module addr_decode (
  input  [7:0] addr,
  output is_ram,
  output is_per,
  output [15:0] per_sel
);

  dec4to16 pdec (.a(addr[3:0]), .en(is_per), .y(per_sel));
  and and_1 (is_per, addr[7], addr[6], addr[5], addr[4]);
  not not_1 (is_ram, addr[7]);

  // Other names for the same wires on the sheet: a_0 = addr[0]; a_lo[3:0] = addr[3:0]; a_1 = addr[1]; a_2 = addr[2];
  //   a_3 = addr[3]; a_4 = addr[4]; a_5 = addr[5]; a_6 = addr[6]; a_7 = addr[7]

  // Notes on the sheet:
  //   DATA ADDRESS DECODE
  //   0x00-0x7F RAM ; 0x80-0xEF reserved (read 0, writes ignored) ; 0xF0-0xFF peripherals
endmodule

module mem_stage (
  input  clk,
  input  rst,
  input  v,
  input  memr,
  input  memw,
  input  [7:0] addr,
  input  [7:0] sdata,
  input  [7:0] res,
  input  start,
  input  [1:0] mode,
  input  door_closed,
  input  [7:0] water_level,
  input  [7:0] temp,
  input  [7:0] drum_rpm,
  input  trip,
  input  motor_actual,
  output [7:0] wb_data,
  output [7:0] act,
  output [7:0] display,
  output [7:0] tmr_count,
  output tmr_match,
  output [7:0] tmr_limit,
  output tmr_en,
  output store_commit,
  output ram_we
);

  wire is_per, is_ram, wr_f4, wr_f5, wr_f7, wr_f8;
  wire [7:0] ram_q, rd_f0, rd_f1, rd_f2, rd_f3, rd_f4, rd_f5, rd_f6, rd_f7, rd_f8, rd_f9, rd_ram, rdata;
  wire [15:0] per_sel;

  and and_1 (store_commit, v, memw);
  RAM #(.addrWidth(7), .dataWidth(8), .enables("line"), .line("single"), .databus("bibus"), .trigger("rising"), .clearpin("false"), .\type ("volatile")) DATA_RAM (
    .addr(addr[6:0]), .we(ram_we), .clk(clk), .din(sdata), .dout(ram_q));
  addr_decode adec (.addr(addr), .is_ram(is_ram), .is_per(is_per), .per_sel(per_sel));
  assign rd_f0 = {2'b00, motor_actual, trip, door_closed, start, mode} & {8{per_sel[0]}};  // AND_Gate and_2, 8 bits wide
  assign rd_f3 = drum_rpm & {8{per_sel[3]}};  // AND_Gate and_3, 8 bits wide
  assign rd_f6 = tmr_count & {8{per_sel[6]}};  // AND_Gate and_4, 8 bits wide
  assign rd_f9 = {{7{1'b0}}, tmr_match} & {8{per_sel[9]}};  // AND_Gate and_5, 8 bits wide
  and and_6 (wr_f4, store_commit, per_sel[4]);
  Register #(.width(8), .trigger("rising")) ACT_LATCH (
    .D({1'b0, sdata[6:0]}), .en(wr_f4), .Q(act), .clk(clk), .clr(rst));
  and and_7 (wr_f5, store_commit, per_sel[5]);
  assign rd_f1 = water_level & {8{per_sel[1]}};  // AND_Gate and_8, 8 bits wide
  assign rd_f4 = act & {8{per_sel[4]}};  // AND_Gate and_9, 8 bits wide
  assign rd_f7 = tmr_limit & {8{per_sel[7]}};  // AND_Gate and_10, 8 bits wide
  assign rd_ram = ram_q & {8{is_ram}};  // AND_Gate and_11, 8 bits wide
  and and_12 (ram_we, store_commit, is_ram);
  Register #(.width(8), .trigger("rising")) DISPLAY_REG (.D(sdata), .en(wr_f5), .Q(display), .clk(clk), .clr(rst));
  and and_13 (wr_f7, store_commit, per_sel[7]);
  timer8 timer (
    .clk(clk), .rst(rst), .wr_limit(wr_f7), .wr_ctrl(wr_f8), .wdata(sdata), .count(tmr_count),
    .limit(tmr_limit), .en(tmr_en), .match(tmr_match));
  assign rdata = rd_f0 | rd_f1 | rd_f2 | rd_f3 | rd_f4 | rd_f5 | rd_f6 | rd_f7 | rd_f8 | rd_f9 | rd_ram;  // OR_Gate or_1, 8 bits wide
  assign rd_f5 = display & {8{per_sel[5]}};  // AND_Gate and_14, 8 bits wide
  mux2_8 wb_sel (.a(res), .b(rdata), .s(memr), .y(wb_data));
  and and_15 (wr_f8, store_commit, per_sel[8]);
  assign rd_f2 = temp & {8{per_sel[2]}};  // AND_Gate and_16, 8 bits wide
  assign rd_f8 = {{7{1'b0}}, tmr_en} & {8{per_sel[8]}};  // AND_Gate and_17, 8 bits wide

  // Other names for the same wires on the sheet: act_d[6:0] = sdata[6:0]; sd_0 = sdata[0]; sd_1 = sdata[1];
  //   sd_2 = sdata[2]; sd_3 = sdata[3]; sd_4 = sdata[4]; sd_5 = sdata[5]; sd_6 = sdata[6]; ram_addr[6:0] = addr[6:0];
  //   ctrl_rd[0] = tmr_en; in_status[5:0] = {motor_actual, trip, door_closed, start, mode}; mode_0 = mode[0];
  //   mode_1 = mode[1]; sel0_bus[7:0] = {8{per_sel[0]}}; sel_0 = per_sel[0]; sel1_bus[7:0] = {8{per_sel[1]}};
  //   sel_1 = per_sel[1]; sel3_bus[7:0] = {8{per_sel[3]}}; sel_3 = per_sel[3]; sel4_bus[7:0] = {8{per_sel[4]}};
  //   sel_4 = per_sel[4]; sel6_bus[7:0] = {8{per_sel[6]}}; sel_6 = per_sel[6]; sel7_bus[7:0] = {8{per_sel[7]}};
  //   sel_7 = per_sel[7]; sel9_bus[7:0] = {8{per_sel[9]}}; sel_9 = per_sel[9]; sel_10 = per_sel[10];
  //   sel_11 = per_sel[11]; sel_12 = per_sel[12]; sel_13 = per_sel[13]; sel_14 = per_sel[14]; sel_15 = per_sel[15];
  //   ram_bus[7:0] = {8{is_ram}}; sd_7 = sdata[7]; sel2_bus[7:0] = {8{per_sel[2]}}; sel_2 = per_sel[2];
  //   sel5_bus[7:0] = {8{per_sel[5]}}; sel_5 = per_sel[5]; sel8_bus[7:0] = {8{per_sel[8]}}; sel_8 = per_sel[8];
  //   status_rd[0] = tmr_match

  // Notes on the sheet:
  //   MEM STAGE: data RAM + memory-mapped I/O
  //   All writes qualified: store_commit = v & memw (one MEM cycle per store).  Reads are combinational.
  //   F0 IN  F1 WATER_LEVEL  F2 TEMP  F3 DRUM_RPM  F4 ACT  F5 DISPLAY  F6 T_COUNT  F7 T_LIMIT  F8 T_CTRL  F9 T_STATUS
endmodule

module if_stage (
  input  clk,
  input  rst,
  input  pc_en,
  input  taken,
  input  [7:0] target,
  output [7:0] pc,
  output [15:0] ir
);

  wire pc_wrap;
  wire [7:0] pc_next, pc_plus1;

  inc8 pc_inc (.a(pc), .y(pc_plus1), .co(pc_wrap));
  ROM #(.addrWidth(8), .dataWidth(16)) IMEM (.addr(pc), .data(ir));
  Register #(.width(8), .trigger("rising")) u_PC (.D(pc_next), .en(pc_en), .Q(pc), .clk(clk), .clr(rst));
  mux2_8 pc_sel (.a(pc_plus1), .b(target), .s(taken), .y(pc_next));

  // Notes on the sheet:
  //   IF STAGE: PC + instruction ROM
  //   PC <= taken ? target : PC+1 when pc_en ; PC cleared by reset ; ROM is 256 x 16, word addressed
  //   contents of IMEM (hex, n*v repeats v):
  //   12a5 1400 7280 125a 147f 7280 1233 1480 7280 1244 14ef 7280 1255 14fc 7280 1266 14f1 7280 1277 14f6
  //   7280 12c3 14f5 7280 1400 6680 147f 6880 1480 6a80 14ef 6c80 1e50 77c0 8e01 79c0 8e01 7bc0 8e01 7dc0
  //   146f 6680 14fc 6880 14f1 6a80 14f5 6c80 8e01 77c0 8e01 79c0 8e01 7bc0 8e01 7dc0 f000 0 0 0 0 0 0 0 0
  //   0 0 0 0 0 0 0 0 0 0 0 0 0 0 0 0 0 0 0 0 0 0 0 0 0 0 0 0 0 0 0 0 0 0 0 0 0 0 0 0 0 0 0 0 0 0 0 0 0 0
  //   0 0 0 0 0 0 0 0 0 0 0 0 0 0 0 0 0 0 0 0 0 0 0 0 0 0 0 0 0 0 0 0 0 0 0 0 0 0 0 0 0 0 0 0 0 0 0 0 0 0
  //   0 0 0 0 0 0 0 0 0 0 0 0 0 0 0 0 0 0 0 0 0 0 0 0 0 0 0 0 0 0 0 0 0 0 0 0 0 0 0 0 0 0 0 0 0 0 0 0 0 0
  //   0 0 0 0 0 0 0 0 0 0 0 0 0 0 0 0 0 0 0 0 0 0 0 0 0 0 0 0 0 0 0 0 0 0 0 0 0 0 0 0 0
endmodule

module mcu_core (
  input  clk,
  input  rst,
  input  start,
  input  [1:0] mode,
  input  door_closed,
  input  [7:0] water_level,
  input  [7:0] temp,
  input  [7:0] drum_rpm,
  output valve_in,
  output heater,
  output motor_en,
  output motor_dir,
  output pump_out,
  output door_lock,
  output buzzer,
  output [7:0] display,
  output motor_actual,
  output trip,
  output halted,
  output [7:0] pc,
  output ifid_v,
  output idex_v,
  output exm_v,
  output mwb_v,
  output [7:0] ifid_pc,
  output [7:0] idex_pc,
  output [7:0] exm_pc,
  output [7:0] mwb_pc,
  output stall,
  output flush,
  output [1:0] fwd_a,
  output [1:0] fwd_b,
  output rf_we,
  output [2:0] rf_wa,
  output [7:0] rf_wd,
  output st_commit,
  output [7:0] st_addr,
  output [7:0] st_data,
  output [7:0] tmr_count,
  output tmr_match
);

  wire ex_a_zero, exm_memr, exm_memw, exm_regw, halt_ex, halted_d, id_aluimm, id_alusub, id_beqz, id_bnez,
       id_halt, id_jmp, id_memr, id_memw, id_regw, id_uses_a, id_uses_b, idex_aluimm, idex_alusub, idex_beqz,
       idex_bnez, idex_halt, idex_jmp, idex_memr, idex_memw, idex_regw, idex_vd, ifid_en, ifid_vd, mwb_regw,
       pc_en, ram_we, stall_eff, taken, tmr_en;
  wire [1:0] id_aluop, idex_aluop;
  wire [2:0] exm_rd, id_rd, idex_rb, idex_rd, mwb_rd;
  wire [2:2] id_rb;
  wire [3:0] id_op;
  wire [7:0] a_fwd, act, b_fwd, ex_res, exm_addr, exm_res, exm_sdata, id_imm, id_qa, id_qb, idex_a, idex_b,
       idex_imm, mem_wb_data, mwb_wdata, R0, R1, R2, R3, R4, R5, R6, R7, tmr_limit;
  wire [15:0] ir_fetch;

  if_stage IF (.clk(clk), .rst(rst), .pc_en(pc_en), .taken(taken), .target(idex_imm), .pc(pc), .ir(ir_fetch));
  control_dec CTRL (
    .op(id_op), .regw(id_regw), .aluimm(id_aluimm), .aluop(id_aluop), .alusub(id_alusub), .memr(id_memr),
    .memw(id_memw), .beqz(id_beqz), .bnez(id_bnez), .jmp(id_jmp), .halt(id_halt), .uses_a(id_uses_a),
    .uses_b(id_uses_b));
  id_ex ID_EX (
    .clk(clk), .rst(rst), .v_d(idex_vd), .pc_d(ifid_pc), .rd_d(id_rd), .rb_d({id_rb[2], id_imm[7:6]}),
    .a_d(id_qa), .b_d(id_qb), .imm_d(id_imm), .aluop_d(id_aluop), .alusub_d(id_alusub), .aluimm_d(id_aluimm),
    .regw_d(id_regw), .memr_d(id_memr), .memw_d(id_memw), .beqz_d(id_beqz), .bnez_d(id_bnez), .jmp_d(id_jmp),
    .halt_d(id_halt), .v(idex_v), .pc(idex_pc), .rd(idex_rd), .rb(idex_rb), .a(idex_a), .b(idex_b),
    .imm(idex_imm), .aluop(idex_aluop), .alusub(idex_alusub), .aluimm(idex_aluimm), .regw(idex_regw),
    .memr(idex_memr), .memw(idex_memw), .beqz(idex_beqz), .bnez(idex_bnez), .jmp(idex_jmp), .halt(idex_halt));
  mem_stage MEM (
    .clk(clk), .rst(rst), .v(exm_v), .memr(exm_memr), .memw(exm_memw), .addr(exm_addr), .sdata(exm_sdata),
    .res(exm_res), .start(start), .mode(mode), .door_closed(door_closed), .water_level(water_level),
    .temp(temp), .drum_rpm(drum_rpm), .trip(trip), .motor_actual(motor_actual), .wb_data(mem_wb_data),
    .act(act), .display(display), .tmr_count(tmr_count), .tmr_match(tmr_match), .tmr_limit(tmr_limit),
    .tmr_en(tmr_en), .store_commit(st_commit), .ram_we(ram_we));
  or or_1 (motor_en, act[2], act[2]);
  mem_wb MEM_WB (
    .clk(clk), .rst(rst), .v_d(exm_v), .pc_d(exm_pc), .rd_d(exm_rd), .wdata_d(mem_wb_data),
    .regw_d(exm_regw), .v(mwb_v), .pc(mwb_pc), .rd(mwb_rd), .wdata(mwb_wdata), .regw(mwb_regw));
  or or_2 (motor_dir, act[3], act[3]);
  regfile8x8 RF (
    .clk(clk), .ra(id_rd), .rb({id_rb[2], id_imm[7:6]}), .wa(rf_wa), .wd(rf_wd), .we(rf_we), .qa(id_qa),
    .qb(id_qb), .r0(R0), .r1(R1), .r2(R2), .r3(R3), .r4(R4), .r5(R5), .r6(R6), .r7(R7));
  fwd_unit FWD (
    .src_a(idex_rd), .src_b(idex_rb), .a_rf(idex_a), .b_rf(idex_b), .exm_v(exm_v), .exm_regw(exm_regw),
    .exm_memr(exm_memr), .exm_rd(exm_rd), .exm_res(exm_res), .mwb_v(mwb_v), .mwb_regw(mwb_regw),
    .mwb_rd(mwb_rd), .mwb_wd(mwb_wdata), .a_fwd(a_fwd), .b_fwd(b_fwd), .fwd_a(fwd_a), .fwd_b(fwd_b));
  and and_1 (rf_we, mwb_v, mwb_regw);
  if_id IF_ID (
    .clk(clk), .rst(rst), .en(ifid_en), .v_d(ifid_vd), .pc_d(pc), .ir_d(ir_fetch), .v(ifid_v), .pc(ifid_pc),
    .ir({id_op, id_rd, id_rb[2], id_imm}));
  or or_3 (pump_out, act[4], act[4]);
  assign st_addr = exm_addr | exm_addr;  // OR_Gate or_4, 8 bits wide
  assign rf_wa = mwb_rd | mwb_rd;  // OR_Gate or_5, 3 bits wide
  hazard_unit HAZ (
    .ifid_v(ifid_v), .ra(id_rd), .rb({id_rb[2], id_imm[7:6]}), .uses_a(id_uses_a), .uses_b(id_uses_b),
    .idex_v(idex_v), .idex_memr(idex_memr), .idex_rd(idex_rd), .stall(stall));
  ex_stage EX (
    .a(a_fwd), .b(b_fwd), .imm(idex_imm), .aluop(idex_aluop), .alusub(idex_alusub), .aluimm(idex_aluimm),
    .v(idex_v), .beqz(idex_beqz), .bnez(idex_bnez), .jmp(idex_jmp), .halt(idex_halt), .res(ex_res),
    .taken(taken), .halt_ex(halt_ex), .a_zero(ex_a_zero));
  or or_6 (door_lock, act[5], act[5]);
  assign st_data = exm_sdata | exm_sdata;  // OR_Gate or_7, 8 bits wide
  assign rf_wd = mwb_wdata | mwb_wdata;  // OR_Gate or_8, 8 bits wide
  pipe_ctrl PCTL (
    .stall(stall), .taken(taken), .halt_ex(halt_ex), .halted(halted), .ifid_v(ifid_v), .kill(flush),
    .stall_eff(stall_eff), .pc_en(pc_en), .ifid_en(ifid_en), .ifid_vd(ifid_vd), .idex_vd(idex_vd),
    .halted_d(halted_d));
  or or_9 (buzzer, act[6], act[6]);
  ex_mem EX_MEM (
    .clk(clk), .rst(rst), .v_d(idex_v), .pc_d(idex_pc), .rd_d(idex_rd), .res_d(ex_res), .addr_d(b_fwd),
    .sdata_d(a_fwd), .regw_d(idex_regw), .memr_d(idex_memr), .memw_d(idex_memw), .v(exm_v), .pc(exm_pc),
    .rd(exm_rd), .res(exm_res), .addr(exm_addr), .sdata(exm_sdata), .regw(exm_regw), .memr(exm_memr),
    .memw(exm_memw));
  safety_ilock SAFETY (
    .clk(clk), .rst(rst), .motor_req(act[2]), .door_closed(door_closed), .start(start),
    .motor_actual(motor_actual), .trip(trip));
  or or_10 (valve_in, act[0], act[0]);
  Register #(.width(1), .trigger("rising")) u_HALTED (.D(halted_d), .Q(halted), .clk(clk), .clr(rst));  // open: en
  or or_11 (heater, act[1], act[1]);

  // Other names for the same wires on the sheet: act_0 = act[0]; act_1 = act[1]; act_2 = act[2]; act_3 = act[3];
  //   act_4 = act[4]; act_5 = act[5]; act_6 = act[6]; act_7 = act[7];
  //   ifid_ir[15:0] = {id_op, id_rd, id_rb[2], id_imm}; id_rb[1:0] = id_imm[7:6]

  // Notes on the sheet:
  //   MCU CORE: IF | ID | EX | MEM | WB
  //   Pipeline: IF -> [IF/ID] -> ID -> [ID/EX] -> EX -> [EX/MEM] -> MEM -> [MEM/WB] -> WB
  //   All architectural writes are gated by the stage valid bit (RF: mwb_v&regw, RAM/IO: exm_v&memw).
endmodule
